// Logisim project Datapath.circ as structural Verilog
module Datapath (
  input  clk
);

  wire alu_1_carry, alu_1_zero, control_unit_1_alusrc, control_unit_1_extop, control_unit_1_flagen,
       control_unit_1_memrd, control_unit_1_memwr, control_unit_1_rbsrc, control_unit_1_regwr, or_1_out,
       Zero_flag_q;
  wire [1:0] control_unit_1_aluop, control_unit_1_regdst, control_unit_1_wbdata, pc_unit_1_pcmux;
  wire [2:0] multiplexer_2_out, multiplexer_3_out;
  wire [4:0] instructionmemory_1_instruction_2;
  wire [19:0] bit_extender_2_out;
  wire [23:0] adder_1_out, adder_2_out, adder_3_out, alu_1_output, bit_extender_1_out, datamemory_1_data_out,
       extender_1_output, instructionmemory_1_instruction, multiplexer_1_out, multiplexer_4_out,
       multiplexer_5_out, PC_q, register_file_1_busa, register_file_1_busb;

  Multiplexer #(.select(2), .width(24), .enable("false")) multiplexer_1 (
    .in0(adder_1_out), .in1(register_file_1_busa), .in2(adder_3_out), .in3(adder_2_out),
    .out(multiplexer_1_out), .sel(pc_unit_1_pcmux));
  Register #(.width(24)) PC (.D(multiplexer_1_out), .Q(PC_q), .clk(clk), .clr(1'b0));  // open: en
  PC_Unit pc_unit_1 (.PCmux(pc_unit_1_pcmux), .opcode(instructionmemory_1_instruction_2), .zero(Zero_flag_q));
  Adder #(.width(24)) adder_1 (.a(24'h1), .b(PC_q), .out(adder_1_out));  // open: cin, cout
  InstructionMemory instructionmemory_1 (
    .Address(PC_q),
    .Instruction({instructionmemory_1_instruction[23:22], instructionmemory_1_instruction_2, instructionmemory_1_instruction[16:0]}));
  assign bit_extender_1_out = {{7{instructionmemory_1_instruction[16]}}, instructionmemory_1_instruction[16:0]};  // Bit_Extender bit_extender_1
  Multiplexer #(.width(3), .enable("false")) multiplexer_2 (
    .in0(instructionmemory_1_instruction[9:7]), .in1(multiplexer_3_out), .out(multiplexer_2_out),
    .sel(control_unit_1_rbsrc));
  Multiplexer #(.select(2), .width(3), .enable("false")) multiplexer_3 (
    .in0(instructionmemory_1_instruction[15:13]), .in1(3'b111), .in2(3'b001), .out(multiplexer_3_out),
    .sel(control_unit_1_regdst));  // open: in3
  Adder #(.width(24)) adder_2 (.a(PC_q), .b(bit_extender_1_out), .out(adder_2_out));  // open: cin, cout
  Extender extender_1 (
    .IMM10(instructionmemory_1_instruction[9:0]), .ExtOP(control_unit_1_extop), .\output (extender_1_output));
  Register_File register_file_1 (
    .RegWrite(control_unit_1_regwr), .RW(multiplexer_3_out), .BusA(register_file_1_busa),
    .RA(instructionmemory_1_instruction[12:10]), .BusB(register_file_1_busb), .BusW(multiplexer_5_out),
    .RB(multiplexer_2_out), .Clk(clk));
  Control_Unit control_unit_1 (
    .opcode(instructionmemory_1_instruction_2), .SF(instructionmemory_1_instruction[16]),
    .RegDst(control_unit_1_regdst), .RegWr(control_unit_1_regwr), .ExtOp(control_unit_1_extop),
    .ALUSrc(control_unit_1_alusrc), .MemRd(control_unit_1_memrd), .MemWr(control_unit_1_memwr),
    .WBdata(control_unit_1_wbdata), .ALUOp(control_unit_1_aluop), .FlagEN(control_unit_1_flagen),
    .Cond(instructionmemory_1_instruction[23:22]), .zero(Zero_flag_q), .RBSrc(control_unit_1_rbsrc));
  Adder #(.width(24)) adder_3 (.a(adder_1_out), .b(extender_1_output), .out(adder_3_out));  // open: cin, cout
  Multiplexer #(.width(24), .enable("false")) multiplexer_4 (
    .in0(register_file_1_busb), .in1(extender_1_output), .out(multiplexer_4_out), .sel(control_unit_1_alusrc));
  ALU alu_1 (
    .scr1(register_file_1_busa), .sec2(multiplexer_4_out), .Aluop(control_unit_1_aluop),
    .\output (alu_1_output), .zero(alu_1_zero), .carry(alu_1_carry));
  or or_1 (or_1_out, alu_1_zero, alu_1_carry);
  Register #(.width(1)) Zero_flag (.D(or_1_out), .en(control_unit_1_flagen), .Q(Zero_flag_q), .clk(clk), .clr(1'b0));
  assign bit_extender_2_out = {{3{instructionmemory_1_instruction[16]}}, instructionmemory_1_instruction[16:0]};  // Bit_Extender bit_extender_2
  DataMemory datamemory_1 (
    .Address(alu_1_output), .Data_out(datamemory_1_data_out), .MemRead(control_unit_1_memrd), .CLK(clk),
    .MemWrite(control_unit_1_memwr), .Data_in(register_file_1_busb));
  Multiplexer #(.select(2), .width(24), .enable("false")) multiplexer_5 (
    .in0(alu_1_output), .in1(datamemory_1_data_out), .in2(adder_1_out), .in3({bit_extender_2_out, 4'b0000}),
    .out(multiplexer_5_out), .sel(control_unit_1_wbdata));
endmodule

module ALU (
  input  [23:0] scr1,
  input  [23:0] sec2,
  input  [1:0] Aluop,
  output [23:0] \output ,
  output zero,
  output carry
);

  wire and_2_out, subtractor_1_bout;
  wire [23:0] adder_1_out, and_1_out, multiplexer_1_out, subtractor_1_out;

  assign and_1_out = scr1 & sec2;  // AND_Gate and_1, 24 bits wide
  Adder #(.width(24)) adder_1 (.a(scr1), .b(sec2), .out(adder_1_out));  // open: cin, cout
  Subtractor #(.width(24)) subtractor_1 (
    .a(scr1), .b(sec2), .out(subtractor_1_out), .bout(subtractor_1_bout));  // open: bin
  Multiplexer #(.select(2), .width(24), .enable("false")) multiplexer_1 (
    .in0(and_1_out), .in1(adder_1_out), .in2(subtractor_1_out), .in3(scr1), .out(multiplexer_1_out),
    .sel(Aluop));
  and and_2 (and_2_out, Aluop[0], Aluop[1]);
  Multiplexer #(.enable("false")) multiplexer_2 (.in0(1'b0), .in1(subtractor_1_bout), .out(carry), .sel(and_2_out));
  Multiplexer #(.width(24), .enable("false")) multiplexer_3 (
    .in0(multiplexer_1_out), .in1(sec2), .out(\output ), .sel(carry));
  nor nor_1 (zero, multiplexer_1_out[0], multiplexer_1_out[1], multiplexer_1_out[2], multiplexer_1_out[3], multiplexer_1_out[4], multiplexer_1_out[5], multiplexer_1_out[6], multiplexer_1_out[7], multiplexer_1_out[8], multiplexer_1_out[9], multiplexer_1_out[10], multiplexer_1_out[11], multiplexer_1_out[12], multiplexer_1_out[13], multiplexer_1_out[14], multiplexer_1_out[15], multiplexer_1_out[16], multiplexer_1_out[17], multiplexer_1_out[18], multiplexer_1_out[19], multiplexer_1_out[20], multiplexer_1_out[21], multiplexer_1_out[22], multiplexer_1_out[23]);
endmodule

// Reg File
module Register_File (
  input  RegWrite,
  input  [2:0] RW,
  input  [2:0] RA,
  input  [23:0] BusW,
  input  [2:0] RB,
  input  Clk,
  output [23:0] BusA,
  output [23:0] BusB
);

  wire and_1_out, and_2_out, and_3_out, and_4_out, and_5_out, and_6_out, and_7_out, decoder_1_out1,
       decoder_1_out2, decoder_1_out3, decoder_1_out4, decoder_1_out5, decoder_1_out6, decoder_1_out7;
  wire [23:0] register_1_q, register_2_q, register_3_q, register_4_q, register_5_q, register_6_q,
       register_7_q;

  Decoder #(.select(3), .enable("false")) decoder_1 (
    .out1(decoder_1_out1), .out2(decoder_1_out2), .out3(decoder_1_out3), .out4(decoder_1_out4),
    .out5(decoder_1_out5), .out6(decoder_1_out6), .out7(decoder_1_out7), .sel(RW));  // open: out0
  and and_1 (and_1_out, RegWrite, decoder_1_out1);
  and and_2 (and_2_out, RegWrite, decoder_1_out2);
  and and_3 (and_3_out, RegWrite, decoder_1_out3);
  and and_4 (and_4_out, RegWrite, decoder_1_out4);
  and and_5 (and_5_out, RegWrite, decoder_1_out5);
  and and_6 (and_6_out, RegWrite, decoder_1_out6);
  and and_7 (and_7_out, RegWrite, decoder_1_out7);
  Register #(.width(24)) register_1 (.D(BusW), .en(and_1_out), .Q(register_1_q), .clk(Clk), .clr(1'b0));
  Register #(.width(24)) register_2 (.D(BusW), .en(and_2_out), .Q(register_2_q), .clk(Clk), .clr(1'b0));
  Register #(.width(24)) register_3 (.D(BusW), .en(and_3_out), .Q(register_3_q), .clk(Clk), .clr(1'b0));
  Register #(.width(24)) register_4 (.D(BusW), .en(and_4_out), .Q(register_4_q), .clk(Clk), .clr(1'b0));
  Register #(.width(24)) register_5 (.D(BusW), .en(and_5_out), .Q(register_5_q), .clk(Clk), .clr(1'b0));
  Register #(.width(24)) register_6 (.D(BusW), .en(and_6_out), .Q(register_6_q), .clk(Clk), .clr(1'b0));
  Register #(.width(24)) register_7 (.D(BusW), .en(and_7_out), .Q(register_7_q), .clk(Clk), .clr(1'b0));
  Multiplexer #(.select(3), .width(24)) multiplexer_1 (
    .in0({24{1'b0}}), .in1(register_1_q), .in2(register_2_q), .in3(register_3_q), .in4(register_4_q),
    .in5(register_5_q), .in6(register_6_q), .in7(register_7_q), .out(BusA), .sel(RA), .en(1'b1));
  Multiplexer #(.select(3), .width(24)) multiplexer_2 (
    .in0({24{1'b0}}), .in1(register_1_q), .in2(register_2_q), .in3(register_3_q), .in4(register_4_q),
    .in5(register_5_q), .in6(register_6_q), .in7(register_7_q), .out(BusB), .sel(RB), .en(1'b1));
endmodule

// Data Mem
module DataMemory (
  input  [23:0] Address,
  input  [23:0] Data_in,
  input  MemRead,
  input  MemWrite,
  input  CLK,
  output [23:0] Data_out
);

  wire not_1_out, not_2_out, or_1_out;
  wire [23:0] ram_1_data;

  not not_1 (not_1_out, MemWrite);
  or or_1 (or_1_out, MemRead, MemWrite);
  RAM #(.addrWidth(24), .dataWidth(24)) ram_1 (
    .addr(Address), .data(ram_1_data), .sel(or_1_out), .clk(CLK), .ld(not_1_out), .clr(1'b0));
  assign ram_1_data = MemWrite ? Data_in : 24'bz;  // Controlled_Buffer controlled_buffer_1
  assign Data_out = not_2_out ? ram_1_data : 24'bz;  // Controlled_Buffer controlled_buffer_2
  not not_2 (not_2_out, MemWrite);
endmodule

// Ins Mem
module InstructionMemory (
  input  [23:0] Address,
  output [23:0] Instruction
);

  RAM #(.addrWidth(24), .dataWidth(24), .bus("asynch")) ram_1 (
    .addr(Address), .data(Instruction), .sel(1'b1), .ld(1'b1), .clr(1'b0));
endmodule

module Extender (
  input  [9:0] IMM10,
  input  ExtOP,
  output [23:0] \output 
);

  wire [23:0] bit_extender_1_out, bit_extender_2_out;

  assign bit_extender_1_out = {{14{1'b0}}, IMM10};  // Bit_Extender bit_extender_1
  assign bit_extender_2_out = {{14{IMM10[9]}}, IMM10};  // Bit_Extender bit_extender_2
  Multiplexer #(.width(24), .enable("false")) multiplexer_1 (
    .in0(bit_extender_1_out), .in1(bit_extender_2_out), .out(\output ), .sel(ExtOP));
endmodule

// Main Unit
module Control_Unit (
  input  [4:0] opcode,
  input  [1:0] Cond,
  input  zero,
  input  SF,
  output [1:0] RegDst,
  output RBSrc,
  output RegWr,
  output ExtOp,
  output ALUSrc,
  output MemRd,
  output MemWr,
  output [1:0] WBdata,
  output [1:0] ALUOp,
  output FlagEN
);

  wire ADDI_out, and_2_out, and_3_out, and_4_out, and_5_out, AND_out, ANDI_out, BEQ_out, CAS_out, CMP_out,
       J_out, JAL_out, JR_out, LUI_out, LW_out, LWS_out, nor_1_out, nor_2_out, not_1_out, or_1_out, or_2_out,
       or_3_out, or_4_out, or_5_out, or_6_out, or_7_out, or_8_out, SUB_out, SW_out;

  and AND (AND_out, ~opcode[0], ~opcode[1], ~opcode[2], ~opcode[3], ~opcode[4]);  // AND_Gate
  and CAS (CAS_out, opcode[0], ~opcode[1], ~opcode[2], ~opcode[3], ~opcode[4]);  // AND_Gate
  and SUB (SUB_out, ~opcode[0], ~opcode[1], opcode[2], ~opcode[3], ~opcode[4]);  // AND_Gate
  and LWS (LWS_out, ~opcode[0], opcode[1], ~opcode[2], ~opcode[3], ~opcode[4]);  // AND_Gate
  and CMP (CMP_out, opcode[0], ~opcode[1], opcode[2], ~opcode[3], ~opcode[4]);  // AND_Gate
  and JR (JR_out, ~opcode[0], opcode[1], opcode[2], ~opcode[3], ~opcode[4]);  // AND_Gate
  and ADDI (ADDI_out, ~opcode[0], ~opcode[1], ~opcode[2], opcode[3], ~opcode[4]);  // AND_Gate
  and ANDI (ANDI_out, opcode[0], opcode[1], opcode[2], ~opcode[3], ~opcode[4]);  // AND_Gate
  and LW (LW_out, opcode[0], ~opcode[1], ~opcode[2], opcode[3], ~opcode[4]);  // AND_Gate
  and SW (SW_out, ~opcode[0], opcode[1], ~opcode[2], opcode[3], ~opcode[4]);  // AND_Gate
  and BEQ (BEQ_out, opcode[0], opcode[1], ~opcode[2], opcode[3], ~opcode[4]);  // AND_Gate
  and J (J_out, ~opcode[0], ~opcode[1], opcode[2], opcode[3], ~opcode[4]);  // AND_Gate
  and JAL (JAL_out, opcode[0], ~opcode[1], opcode[2], opcode[3], ~opcode[4]);  // AND_Gate
  and LUI (LUI_out, ~opcode[0], opcode[1], opcode[2], opcode[3], ~opcode[4]);  // AND_Gate
  and and_2 (and_2_out, SUB_out, SF);
  and and_3 (and_3_out, ~Cond[1], ~Cond[0]);  // AND_Gate
  or or_1 (or_1_out, SW_out, BEQ_out);
  nor nor_1 (nor_1_out, J_out, BEQ_out, SW_out, JR_out, CMP_out);
  not not_1 (not_1_out, ANDI_out);
  or or_2 (or_2_out, SW_out, LW_out, ADDI_out, ANDI_out);
  or or_3 (or_3_out, LW_out, LWS_out);
  or or_4 (or_4_out, LUI_out, LW_out, LWS_out);
  or or_5 (or_5_out, JAL_out, LUI_out);
  nor nor_2 (nor_2_out, BEQ_out, ANDI_out, SUB_out, AND_out);
  or or_6 (or_6_out, BEQ_out, CMP_out, SUB_out, CAS_out);
  or or_7 (or_7_out, BEQ_out, CMP_out, and_2_out);
  and and_4 (and_4_out, ~Cond[1], Cond[0], zero);  // AND_Gate
  and and_5 (and_5_out, Cond[1], ~Cond[0], ~zero);  // AND_Gate
  or or_8 (or_8_out, and_3_out, and_4_out, and_5_out);
  and and_6 (RegDst[0], or_8_out, JAL_out);
  and and_7 (RegDst[1], LUI_out, or_8_out);
  and and_8 (RBSrc, or_1_out, or_8_out);
  and and_9 (RegWr, nor_1_out, or_8_out);
  and and_10 (ExtOp, not_1_out, or_8_out);
  and and_11 (ALUSrc, or_2_out, or_8_out);
  and and_12 (MemRd, or_3_out, or_8_out);
  and and_13 (MemWr, SW_out, or_8_out);
  and and_14 (WBdata[0], or_4_out, or_8_out);
  and and_15 (WBdata[1], or_5_out, or_8_out);
  and and_16 (ALUOp[0], nor_2_out, or_8_out);
  and and_17 (ALUOp[1], or_6_out, or_8_out);
  and and_18 (FlagEN, or_8_out, or_7_out);
endmodule

// PC
module PC_Unit (
  input  [4:0] opcode,
  input  zero,
  output [1:0] PCmux
);

  wire and_1_out, BEQ_out, J_out, JAL_out, JR_out;

  or or_1 (PCmux[0], JR_out, JAL_out, J_out);
  and and_1 (and_1_out, BEQ_out, zero);
  or or_2 (PCmux[1], and_1_out, JAL_out, J_out);
  and BEQ (BEQ_out, ~opcode[4], opcode[3], ~opcode[2], opcode[1], opcode[0]);  // AND_Gate
  and JR (JR_out, ~opcode[4], ~opcode[3], opcode[2], opcode[1], ~opcode[0]);  // AND_Gate
  and J (J_out, ~opcode[4], opcode[3], opcode[2], ~opcode[1], ~opcode[0]);  // AND_Gate
  and JAL (JAL_out, ~opcode[4], opcode[3], opcode[2], ~opcode[1], opcode[0]);  // AND_Gate
endmodule
